// Logisim project Decodificador7segmentos.circ as structural Verilog: 1 circuit, main circuit decodificador
module decodificador (
  input  D,
  input  C,
  input  B,
  input  A
);

  wire and_1_out, and_2_out, and_3_out, and_4_out, and_5_out, and_6_out, and_7_out, and_8_out, and_9_out,
       and_10_out, and_11_out, and_12_out, and_13_out, and_14_out, and_15_out, and_16_out, and_17_out,
       and_18_out, and_19_out, and_20_out, and_21_out, and_22_out, and_23_out, and_24_out, and_25_out,
       and_26_out, and_27_out, and_28_out, and_29_out, and_30_out, and_31_out, and_32_out, and_33_out,
       and_34_out, and_35_out, and_36_out, not_1_out, not_2_out, not_3_out, not_4_out, not_5_out, not_6_out,
       OK_out, or_1_out, or_2_out, or_3_out, or_4_out, or_5_out, or_6_out, or_7_out;

  not not_1 (not_1_out, C);
  not not_2 (not_2_out, A);
  not not_3 (not_3_out, D);
  not not_4 (not_4_out, B);
  and and_1 (and_1_out, not_1_out, not_2_out);
  and and_2 (and_2_out, not_3_out, B);
  and and_3 (and_3_out, ~D, C, A);  // AND_Gate
  and and_4 (and_4_out, C, B);
  not not_5 (not_5_out, C);
  and and_5 (and_5_out, D, not_5_out, not_6_out);
  not not_6 (not_6_out, B);
  and and_6 (and_6_out, D, ~A);  // AND_Gate
  and OK (OK_out, ~D, ~C);  // AND_Gate
  and and_7 (and_7_out, ~D, ~B, ~A);  // AND_Gate
  and and_8 (and_8_out, ~C, ~B);  // AND_Gate
  and and_9 (and_9_out, ~C, ~A);  // AND_Gate
  and and_10 (and_10_out, ~D, B, A);  // AND_Gate
  and and_11 (and_11_out, D, ~B, A);  // AND_Gate
  and and_12 (and_12_out, ~D, ~B);  // AND_Gate
  and and_13 (and_13_out, ~D, A);  // AND_Gate
  and and_14 (and_14_out, ~B, A);  // AND_Gate
  and and_15 (and_15_out, ~D, C);  // AND_Gate
  and and_16 (and_16_out, D, ~C);  // AND_Gate
  and and_17 (and_17_out, ~D, ~C, ~A);  // AND_Gate
  and and_18 (and_18_out, ~C, B, A);  // AND_Gate
  and and_19 (and_19_out, C, ~B, A);  // AND_Gate
  and and_20 (and_20_out, C, B, ~A);  // AND_Gate
  and and_21 (and_21_out, D, not_4_out);
  and and_22 (and_22_out, ~C, ~A);  // AND_Gate
  and and_23 (and_23_out, B, ~A);  // AND_Gate
  and and_24 (and_24_out, D, B);
  and and_25 (and_25_out, D, C);
  and and_26 (and_26_out, ~C, ~B, ~A);  // AND_Gate
  and and_27 (and_27_out, ~D, C, ~B);  // AND_Gate
  and and_28 (and_28_out, C, B, ~A);  // AND_Gate
  and and_29 (and_29_out, D, ~C);  // AND_Gate
  and and_30 (and_30_out, D, ~A);  // AND_Gate
  and and_31 (and_31_out, D, B);
  and and_32 (and_32_out, ~C, B);  // AND_Gate
  and and_33 (and_33_out, B, ~A);  // AND_Gate
  and and_34 (and_34_out, ~D, C, ~B);  // AND_Gate
  and and_35 (and_35_out, D, ~C);  // AND_Gate
  and and_36 (and_36_out, D, A);
  or or_1 (or_1_out, and_1_out, and_2_out, and_3_out, and_4_out, and_5_out, and_6_out);
  or or_2 (or_2_out, OK_out, and_7_out, and_8_out, and_9_out, and_10_out, and_11_out);
  or or_3 (or_3_out, and_32_out, and_33_out, and_34_out, and_35_out, and_36_out);
  or or_4 (or_4_out, and_12_out, and_13_out, and_14_out, and_15_out, and_16_out, and_16_out);
  or or_5 (or_5_out, and_17_out, and_18_out, and_19_out, and_20_out, and_21_out);
  or or_6 (or_6_out, and_22_out, and_23_out, and_24_out, and_25_out);
  or or_7 (or_7_out, and_26_out, and_27_out, and_28_out, and_29_out, and_30_out, and_31_out);
  _7_Segment_Display u_7_segment_display_1 (
    .g(or_3_out), .f(or_7_out), .a(or_1_out), .b(or_2_out), .e(or_6_out), .d(or_5_out), .c(or_4_out));  // open: dp
endmodule
