// Logisim project Detector_impar.circ as structural Verilog: 2 circuits, main circuit detectorImp
module detectorImp (
  input  [3:0] input0,
  output out_2
);

  wire and_1_out, and_2_out, not_1_out, not_2_out, xor0_1_saida, xor0_2_saida, xor0_3_saida, xor0_4_saida;

  xor0 xor0_1 (.A(input0[0]), .B(input0[1]), .saida(xor0_1_saida));
  xor0 xor0_2 (.A(input0[0]), .B(input0[1]), .saida(xor0_2_saida));
  xor0 xor0_3 (.A(xor0_1_saida), .B(input0[2]), .saida(xor0_3_saida));
  xor0 xor0_4 (.A(xor0_2_saida), .B(input0[2]), .saida(xor0_4_saida));
  not not_1 (not_1_out, input0[3]);
  not not_2 (not_2_out, xor0_4_saida);
  and and_1 (and_1_out, xor0_3_saida, not_1_out);
  and and_2 (and_2_out, not_2_out, input0[3]);
  or or_1 (out_2, and_2_out, and_1_out);
endmodule

module xor0 (
  input  A,
  input  B,
  output saida
);

  wire and_1_out, and_2_out, not_1_out, not_2_out;

  not not_1 (not_1_out, A);
  not not_2 (not_2_out, B);
  and and_1 (and_1_out, not_2_out, A);
  and and_2 (and_2_out, B, not_1_out);
  or or_1 (saida, and_1_out, and_2_out);
endmodule
