// Logisim project MemoriaRam.circ as structural Verilog: 8 circuits, main circuit main
module main (
  input  Enable,
  input  ReadWrite,
  input  [7:0] DataInput,
  input  [2:0] Selector,
  output [7:0] DataOutput
);

  wire and_1_out, CLK_out, decoder1x8_1_o0, decoder1x8_1_o1, decoder1x8_1_o2, decoder1x8_1_o3,
       decoder1x8_1_o4, decoder1x8_1_o5, decoder1x8_1_o6, decoder1x8_1_o7;
  wire [7:0] R0_dataout, R1_dataout, R2_dataout, R3_dataout, R4_dataout, R5_dataout, R6_dataout, R7_dataout;

  Clock CLK (.out(CLK_out));
  and and_1 (and_1_out, ReadWrite, CLK_out);
  Decoder1x8 decoder1x8_1 (
    .Selector(Selector), .WriteEnable(and_1_out), .O0(decoder1x8_1_o0), .O1(decoder1x8_1_o1),
    .O2(decoder1x8_1_o2), .O3(decoder1x8_1_o3), .O4(decoder1x8_1_o4), .O5(decoder1x8_1_o5),
    .O6(decoder1x8_1_o6), .O7(decoder1x8_1_o7));
  Register8Bits R0 (
    .DataIn(DataInput), .WriteEn(decoder1x8_1_o0), .CLK(CLK_out), .Enable(Enable), .DataOut(R0_dataout));
  Register8Bits R1 (
    .DataIn(DataInput), .WriteEn(decoder1x8_1_o1), .CLK(CLK_out), .Enable(Enable), .DataOut(R1_dataout));
  Register8Bits R2 (
    .DataIn(DataInput), .WriteEn(decoder1x8_1_o2), .CLK(CLK_out), .Enable(Enable), .DataOut(R2_dataout));
  Register8Bits R3 (
    .DataIn(DataInput), .WriteEn(decoder1x8_1_o3), .CLK(CLK_out), .Enable(Enable), .DataOut(R3_dataout));
  Register8Bits R4 (
    .DataIn(DataInput), .WriteEn(decoder1x8_1_o4), .CLK(CLK_out), .Enable(Enable), .DataOut(R4_dataout));
  Register8Bits R5 (
    .DataIn(DataInput), .WriteEn(decoder1x8_1_o5), .CLK(CLK_out), .Enable(Enable), .DataOut(R5_dataout));
  Register8Bits R6 (
    .DataIn(DataInput), .WriteEn(decoder1x8_1_o6), .CLK(CLK_out), .Enable(Enable), .DataOut(R6_dataout));
  Register8Bits R7 (
    .DataIn(DataInput), .WriteEn(decoder1x8_1_o7), .CLK(CLK_out), .Enable(Enable), .DataOut(R7_dataout));
  Mult8Bits8x1 mult8bits8x1_1 (
    .Selector(Selector), .I0(R0_dataout), .I1(R1_dataout), .I2(R2_dataout), .I3(R3_dataout), .I4(R4_dataout),
    .I5(R5_dataout), .I6(R6_dataout), .I7(R7_dataout), .O(DataOutput));
endmodule

module Register8Bits (
  input  [7:0] DataIn,
  input  WriteEn,
  input  CLK,
  input  Enable,
  output [7:0] DataOut
);

  wire mult2x1_1_o, mult2x1_2_o, mult2x1_3_o, mult2x1_4_o, mult2x1_5_o, mult2x1_6_o, mult2x1_7_o, mult2x1_8_o;

  Mult2x1 mult2x1_1 (.I0(DataOut[7]), .I1(DataIn[7]), .Selector(WriteEn), .O(mult2x1_1_o));
  Mult2x1 mult2x1_2 (.I0(DataOut[6]), .I1(DataIn[6]), .Selector(WriteEn), .O(mult2x1_2_o));
  DFlipFlop dflipflop_1 (.Enable(Enable), .D(mult2x1_1_o), .CLK(CLK), .Q(DataOut[7]));  // open: Qb
  Mult2x1 mult2x1_3 (.I0(DataOut[5]), .I1(DataIn[5]), .Selector(WriteEn), .O(mult2x1_3_o));
  DFlipFlop dflipflop_2 (.Enable(Enable), .D(mult2x1_2_o), .CLK(CLK), .Q(DataOut[6]));  // open: Qb
  Mult2x1 mult2x1_4 (.I0(DataOut[4]), .I1(DataIn[4]), .Selector(WriteEn), .O(mult2x1_4_o));
  DFlipFlop dflipflop_3 (.Enable(Enable), .D(mult2x1_3_o), .CLK(CLK), .Q(DataOut[5]));  // open: Qb
  Mult2x1 mult2x1_5 (.I0(DataOut[3]), .I1(DataIn[3]), .Selector(WriteEn), .O(mult2x1_5_o));
  DFlipFlop dflipflop_4 (.Enable(Enable), .D(mult2x1_4_o), .CLK(CLK), .Q(DataOut[4]));  // open: Qb
  Mult2x1 mult2x1_6 (.I0(DataOut[2]), .I1(DataIn[2]), .Selector(WriteEn), .O(mult2x1_6_o));
  DFlipFlop dflipflop_5 (.Enable(Enable), .D(mult2x1_5_o), .CLK(CLK), .Q(DataOut[3]));  // open: Qb
  Mult2x1 mult2x1_7 (.I0(DataOut[1]), .I1(DataIn[1]), .Selector(WriteEn), .O(mult2x1_7_o));
  DFlipFlop dflipflop_6 (.Enable(Enable), .D(mult2x1_6_o), .CLK(CLK), .Q(DataOut[2]));  // open: Qb
  Mult2x1 mult2x1_8 (.I0(DataOut[0]), .I1(DataIn[0]), .Selector(WriteEn), .O(mult2x1_8_o));
  DFlipFlop dflipflop_7 (.Enable(Enable), .D(mult2x1_7_o), .CLK(CLK), .Q(DataOut[1]));  // open: Qb
  DFlipFlop dflipflop_8 (.Enable(Enable), .D(mult2x1_8_o), .CLK(CLK), .Q(DataOut[0]));  // open: Qb
endmodule

module Mult8x1 (
  input  [2:0] Selector,
  input  I0,
  input  I1,
  input  I2,
  input  I3,
  input  I4,
  input  I5,
  input  I6,
  input  I7,
  output O
);

  wire and_1_out, and_2_out, and_3_out, and_4_out, and_5_out, and_6_out, and_7_out, and_8_out;

  and and_1 (and_1_out, I0, ~Selector[0], ~Selector[1], ~Selector[2]);  // AND_Gate
  and and_2 (and_2_out, I1, Selector[0], ~Selector[1], ~Selector[2]);  // AND_Gate
  and and_3 (and_3_out, I2, ~Selector[0], Selector[1], ~Selector[2]);  // AND_Gate
  and and_4 (and_4_out, I3, Selector[0], Selector[1], ~Selector[2]);  // AND_Gate
  and and_5 (and_5_out, I4, ~Selector[0], ~Selector[1], Selector[2]);  // AND_Gate
  and and_6 (and_6_out, I5, Selector[0], ~Selector[1], Selector[2]);  // AND_Gate
  and and_7 (and_7_out, I6, ~Selector[0], Selector[1], Selector[2]);  // AND_Gate
  and and_8 (and_8_out, I7, Selector[0], Selector[1], Selector[2]);
  or or_1 (O, and_1_out, and_2_out, and_3_out, and_4_out, and_5_out, and_6_out, and_7_out, and_8_out);
endmodule

module Mult8Bits8x1 (
  input  [7:0] I0,
  input  [7:0] I1,
  input  [7:0] I2,
  input  [7:0] I3,
  input  [7:0] I4,
  input  [7:0] I5,
  input  [7:0] I6,
  input  [7:0] I7,
  input  [2:0] Selector,
  output [7:0] O
);

  Mult8x1 mult8x1_1 (
    .I0(I0[0]), .I1(I1[0]), .I2(I2[0]), .I3(I3[0]), .I4(I4[0]), .I5(I5[0]), .I6(I6[0]), .I7(I7[0]),
    .Selector(Selector), .O(O[0]));
  Mult8x1 mult8x1_2 (
    .I0(I0[1]), .I1(I1[1]), .I2(I2[1]), .I3(I3[1]), .I4(I4[1]), .I5(I5[1]), .I6(I6[1]), .I7(I7[1]),
    .Selector(Selector), .O(O[1]));
  Mult8x1 mult8x1_3 (
    .I0(I0[2]), .I1(I1[2]), .I2(I2[2]), .I3(I3[2]), .I4(I4[2]), .I5(I5[2]), .I6(I6[2]), .I7(I7[2]),
    .Selector(Selector), .O(O[2]));
  Mult8x1 mult8x1_4 (
    .I0(I0[3]), .I1(I1[3]), .I2(I2[3]), .I3(I3[3]), .I4(I4[3]), .I5(I5[3]), .I6(I6[3]), .I7(I7[3]),
    .Selector(Selector), .O(O[3]));
  Mult8x1 mult8x1_5 (
    .I0(I0[4]), .I1(I1[4]), .I2(I2[4]), .I3(I3[4]), .I4(I4[4]), .I5(I5[4]), .I6(I6[4]), .I7(I7[4]),
    .Selector(Selector), .O(O[4]));
  Mult8x1 mult8x1_6 (
    .I0(I0[5]), .I1(I1[5]), .I2(I2[5]), .I3(I3[5]), .I4(I4[5]), .I5(I5[5]), .I6(I6[5]), .I7(I7[5]),
    .Selector(Selector), .O(O[5]));
  Mult8x1 mult8x1_7 (
    .I0(I0[6]), .I1(I1[6]), .I2(I2[6]), .I3(I3[6]), .I4(I4[6]), .I5(I5[6]), .I6(I6[6]), .I7(I7[6]),
    .Selector(Selector), .O(O[6]));
  Mult8x1 mult8x1_8 (
    .I0(I0[7]), .I1(I1[7]), .I2(I2[7]), .I3(I3[7]), .I4(I4[7]), .I5(I5[7]), .I6(I6[7]), .I7(I7[7]),
    .Selector(Selector), .O(O[7]));
endmodule

module Mult2x1 (
  input  I0,
  input  I1,
  input  Selector,
  output O
);

  wire and_1_out, and_2_out;

  and and_1 (and_1_out, I0, ~Selector);  // AND_Gate
  and and_2 (and_2_out, I1, Selector);
  or or_1 (O, and_1_out, and_2_out);
endmodule

module SRLatch (
  input  S,
  input  R,
  output Q,
  output Qb
);

  nand nand_1 (Q, S, Qb);
  nand nand_2 (Qb, Q, R);
endmodule

module DFlipFlop (
  input  D,
  input  Enable,
  input  CLK,
  output Q,
  output Qb
);

  wire and_1_out, nand_1_out, nand_2_out, nand_3_out, nand_4_out, not_1_out, not_2_out, not_3_out,
       srlatch_1_q;

  and and_1 (and_1_out, D, Enable);
  not not_1 (not_1_out, and_1_out);
  nand nand_1 (nand_1_out, and_1_out, CLK);
  nand nand_2 (nand_2_out, CLK, not_1_out);
  not not_2 (not_2_out, CLK);
  SRLatch srlatch_1 (.S(nand_1_out), .R(nand_2_out), .Q(srlatch_1_q));  // open: Qb
  not not_3 (not_3_out, srlatch_1_q);
  nand nand_3 (nand_3_out, srlatch_1_q, not_2_out);
  nand nand_4 (nand_4_out, not_2_out, not_3_out);
  SRLatch srlatch_2 (.S(nand_3_out), .R(nand_4_out), .Q(Q), .Qb(Qb));
endmodule

module Decoder1x8 (
  input  [2:0] Selector,
  input  WriteEnable,
  output O0,
  output O1,
  output O2,
  output O3,
  output O4,
  output O5,
  output O6,
  output O7
);

  wire and_1_out, and_2_out, and_3_out, and_4_out, and_5_out, and_6_out, and_7_out, and_8_out;

  and and_1 (and_1_out, ~Selector[0], ~Selector[1], ~Selector[2]);  // AND_Gate
  and and_2 (and_2_out, Selector[0], ~Selector[1], ~Selector[2]);  // AND_Gate
  and and_3 (and_3_out, ~Selector[0], Selector[1], ~Selector[2]);  // AND_Gate
  and and_4 (and_4_out, Selector[0], Selector[1], ~Selector[2]);  // AND_Gate
  and and_5 (and_5_out, ~Selector[0], ~Selector[1], Selector[2]);  // AND_Gate
  and and_6 (and_6_out, Selector[0], ~Selector[1], Selector[2]);  // AND_Gate
  and and_7 (and_7_out, ~Selector[0], Selector[1], Selector[2]);  // AND_Gate
  and and_8 (and_8_out, Selector[0], Selector[1], Selector[2]);
  and and_9 (O0, and_1_out, WriteEnable);
  and and_10 (O1, and_2_out, WriteEnable);
  and and_11 (O2, and_3_out, WriteEnable);
  and and_12 (O3, and_4_out, WriteEnable);
  and and_13 (O4, and_5_out, WriteEnable);
  and and_14 (O5, and_6_out, WriteEnable);
  and and_15 (O6, and_7_out, WriteEnable);
  and and_16 (O7, and_8_out, WriteEnable);
endmodule
