// Logisim project Multiplexador.circ as structural Verilog: 4 circuits, main circuit Multiplexador4to1
module Multiplexador4to1 (
  input  A,
  input  B,
  input  C,
  input  D,
  input  in_5,
  input  seletor,
  output saida
);

  wire and_1_out, and_2_out, and_3_out, and_4_out, not_1_out;

  not not_1 (not_1_out, in_5);
  and and_1 (and_1_out, A, ~seletor, not_1_out);  // AND_Gate
  and and_2 (and_2_out, B, not_1_out, seletor);
  and and_3 (and_3_out, C, ~seletor, in_5);  // AND_Gate
  and and_4 (and_4_out, D, in_5, seletor);
  or or_1 (saida, and_1_out, and_2_out, and_3_out, and_4_out);
endmodule

module Multiplexador2to1 (
  input  A,
  input  B,
  input  Seletor,
  output saida
);

  wire and_1_out, and_2_out;

  and and_1 (and_1_out, A, ~Seletor);  // AND_Gate
  and and_2 (and_2_out, B, Seletor);
  or or_1 (saida, and_1_out, and_2_out);
endmodule

module Multiplexador4to1_importado (
  input  A,
  input  B,
  input  C,
  input  D,
  input  seletor_2,
  input  seletor,
  output out_7
);

  wire multiplexador2to1_1_saida, multiplexador2to1_2_saida;

  Multiplexador2to1 multiplexador2to1_1 (.A(A), .B(B), .Seletor(seletor), .saida(multiplexador2to1_1_saida));
  Multiplexador2to1 multiplexador2to1_2 (.A(C), .B(D), .Seletor(seletor), .saida(multiplexador2to1_2_saida));
  Multiplexador2to1 multiplexador2to1_3 (
    .A(multiplexador2to1_1_saida), .B(multiplexador2to1_2_saida), .Seletor(seletor_2), .saida(out_7));
endmodule

module Multiplexador8to1 (
  input  in_1,
  input  in_2,
  input  in_3,
  input  in_4,
  input  in_5,
  input  in_6,
  input  seletor,
  input  in_8,
  input  in_9,
  input  in_10,
  input  in_11,
  output \saída 
);

  wire multiplexador4to1_importado_1_out_7, multiplexador4to1_importado_2_out_7;

  Multiplexador4to1_importado multiplexador4to1_importado_1 (
    .A(in_1), .B(in_2), .C(in_3), .D(in_4), .seletor_2(seletor), .seletor(in_5),
    .out_7(multiplexador4to1_importado_1_out_7));
  Multiplexador4to1_importado multiplexador4to1_importado_2 (
    .A(in_8), .B(in_9), .C(in_10), .D(in_11), .seletor_2(seletor), .seletor(in_5),
    .out_7(multiplexador4to1_importado_2_out_7));
  Multiplexador2to1 multiplexador2to1_1 (
    .A(multiplexador4to1_importado_1_out_7), .B(multiplexador4to1_importado_2_out_7), .Seletor(in_6),
    .saida(\saída ));

  // Notes on the sheet:
  //   Inputs
endmodule
