// Logisim project Somador8bitsplus4.circ as structural Verilog: 4 circuits, main circuit somador1bit
module somador1bit (
  input  A0,
  input  B0,
  input  cin,
  output sum,
  output cout
);

  wire and_1_out, and_2_out, and_3_out, xor_1_out;

  and and_1 (and_1_out, A0, B0);
  and and_2 (and_2_out, A0, cin);
  and and_3 (and_3_out, B0, cin);
  xor xor_1 (xor_1_out, A0, B0);
  xor xor_2 (sum, xor_1_out, cin);
  or or_1 (cout, and_1_out, and_2_out, and_3_out);

  // Notes on the sheet:
  //   Input
  //   Saída
  //   cout = carry out
  //   cin= carry in
endmodule

module somador4bitplus4 (
  input  A3,
  input  A2,
  input  A1,
  input  AO,
  input  cin,
  output C3,
  output C2,
  output C1,
  output C0,
  output cout
);

  wire somador1bit_2_cout, somador1bit_3_cout, somador1bit_4_cout;

  somador1bit somador1bit_1 (.A0(A3), .B0(1'b0), .cin(somador1bit_2_cout), .sum(C3), .cout(cout));
  somador1bit somador1bit_2 (.A0(A2), .B0(1'b1), .cin(somador1bit_3_cout), .sum(C2), .cout(somador1bit_2_cout));
  somador1bit somador1bit_3 (.A0(A1), .B0(1'b0), .cin(somador1bit_4_cout), .sum(C1), .cout(somador1bit_3_cout));
  somador1bit somador1bit_4 (.A0(AO), .B0(1'b0), .cin(cin), .sum(C0), .cout(somador1bit_4_cout));

  // Notes on the sheet:
  //   Input
  //   Saída
  //   cout = carry out
  //   cin= carry in
endmodule

module somador4bitplus0 (
  input  A3,
  input  A2,
  input  A1,
  input  AO,
  input  cin,
  output C3,
  output C2,
  output C1,
  output C0,
  output cout
);

  wire somador1bit_2_cout, somador1bit_3_cout, somador1bit_4_cout;

  somador1bit somador1bit_1 (.A0(A3), .B0(1'b0), .cin(somador1bit_2_cout), .sum(C3), .cout(cout));
  somador1bit somador1bit_2 (.A0(A2), .B0(1'b0), .cin(somador1bit_3_cout), .sum(C2), .cout(somador1bit_2_cout));
  somador1bit somador1bit_3 (.A0(A1), .B0(1'b0), .cin(somador1bit_4_cout), .sum(C1), .cout(somador1bit_3_cout));
  somador1bit somador1bit_4 (.A0(AO), .B0(1'b0), .cin(cin), .sum(C0), .cout(somador1bit_4_cout));

  // Notes on the sheet:
  //   Input
  //   Saída
  //   cout = carry out
  //   cin= carry in
endmodule

module somador8bitplus4 (
  input  [7:0] in_1,
  output out_2,
  output out_3,
  output out_4,
  output out_5,
  output out_6,
  output out_7,
  output out_8,
  output out_9,
  output cout
);

  wire somador4bitplus4_1_cout;

  somador4bitplus0 somador4bitplus0_1 (
    .A3(in_1[7]), .A2(in_1[6]), .A1(in_1[5]), .AO(in_1[4]), .cin(somador4bitplus4_1_cout), .C3(out_6),
    .C2(out_7), .C1(out_8), .C0(out_9), .cout(cout));
  somador4bitplus4 somador4bitplus4_1 (
    .A3(in_1[3]), .A2(in_1[2]), .A1(in_1[1]), .AO(in_1[0]), .cin(1'b0), .C3(out_2), .C2(out_3), .C1(out_4),
    .C0(out_5), .cout(somador4bitplus4_1_cout));

  // Notes on the sheet:
  //   Input
  //   cout = carry out
  //   cin= carry in
  //   Saída
endmodule
