// Logisim project ULA.circ as structural Verilog: 18 circuits, main circuit somador
module somador (
  input  A,
  input  B,
  input  cin,
  output result,
  output cout
);

  wire and_1_out, and_2_out, and_3_out, xor_1_out;

  xor xor_1 (xor_1_out, A, B);
  and and_1 (and_1_out, A, B);
  and and_2 (and_2_out, cin, B);
  and and_3 (and_3_out, A, cin);
  xor xor_2 (result, xor_1_out, cin);
  or or_1 (cout, and_1_out, and_2_out, and_3_out);
endmodule

module ula (
  input  [7:0] input1,
  input  [7:0] input2,
  input  [3:0] seletor,
  input  Enable,
  output [7:0] saida0,
  output [7:0] saida1,
  output [7:0] saida2,
  output [7:0] saida2_1,
  output [7:0] saida3,
  output [7:0] saida4,
  output [7:0] saida5,
  output [7:0] saida6,
  output [7:0] saida6_1,
  output [7:0] saida7,
  output [7:0] saida7_1,
  output [7:0] saida8,
  output cout,
  output [7:0] saida9,
  output cout1
);

  wire decoder_1_1_and0, decoder_1_1_nand4, decoder_1_1_nor3, decoder_1_1_not2, decoder_1_1_or1,
       decoder_1_1_shiftd7, decoder_1_1_shifte6, decoder_1_1_soma8, decoder_1_1_sub9, decoder_1_1_xor5;

  decoder_1 decoder_1_1 (
    .seletor(seletor), .Enable(Enable), .AND0(decoder_1_1_and0), .OR1(decoder_1_1_or1),
    .NOT2(decoder_1_1_not2), .NOR3(decoder_1_1_nor3), .NAND4(decoder_1_1_nand4), .XOR5(decoder_1_1_xor5),
    .SHIFTe6(decoder_1_1_shifte6), .SHIFTd7(decoder_1_1_shiftd7), .soma8(decoder_1_1_soma8),
    .sub9(decoder_1_1_sub9));
  AND0 and0_1 (.input1(input1), .input2(input2), .choice(decoder_1_1_and0), .out_4(saida0));
  OR1 or1_1 (.input1(input1), .input2(input2), .choice(decoder_1_1_or1), .out_4(saida1));
  NOT2 not2_1 (.input1(input1), .choice(decoder_1_1_not2), .saida(saida2));
  NOT2 not2_2 (.input1(input2), .choice(decoder_1_1_not2), .saida(saida2_1));
  NOR3 nor3_1 (.input1(input1), .input2(input2), .choice(decoder_1_1_nor3), .out_4(saida3));
  NAND4 nand4_1 (.input1(input1), .input2(input2), .choice(decoder_1_1_nand4), .out_4(saida4));
  XOR5 xor5_1 (.input1(input1), .input2(input2), .choice(decoder_1_1_xor5), .out_4(saida5));
  shifte6_p2 shifte6_p2_1 (
    .input1(input1), .input2(input2), .choice(decoder_1_1_shifte6), .saida1(saida6), .saida2(saida6_1));
  shiftd7_p2 shiftd7_p2_1 (
    .input1(input1), .input2(input2), .choice(decoder_1_1_shiftd7), .saida1(saida7), .saida2(saida7_1));
  somador8bit somador8bit_1 (.input1(input1), .input2(input2), .choice(decoder_1_1_soma8), .saida(saida8), .cout(cout));
  subtrator subtrator_1 (.input1(input1), .input2(input2), .choice(decoder_1_1_sub9), .saida(saida9), .cout(cout1));
endmodule

module somador8bit (
  input  [7:0] input1,
  input  [7:0] input2,
  input  choice,
  output [7:0] saida,
  output cout
);

  wire somador_1_cout, somador_2_cout, somador_3_cout, somador_4_cout, somador_5_cout, somador_6_cout,
       somador_7_cout;
  wire [7:0] multiplexador_1_saida1, multiplexador_1_saida2;

  multiplexador multiplexador_1 (
    .i1(input1), .i2(input2), .choice(choice), .saida1(multiplexador_1_saida1),
    .saida2(multiplexador_1_saida2));
  somador somador_1 (
    .A(multiplexador_1_saida1[0]), .B(multiplexador_1_saida2[0]), .cin(1'b0), .result(saida[0]),
    .cout(somador_1_cout));
  somador somador_2 (
    .A(multiplexador_1_saida1[1]), .B(multiplexador_1_saida2[1]), .cin(somador_1_cout), .result(saida[1]),
    .cout(somador_2_cout));
  somador somador_3 (
    .A(multiplexador_1_saida1[2]), .B(multiplexador_1_saida2[2]), .cin(somador_2_cout), .result(saida[2]),
    .cout(somador_3_cout));
  somador somador_4 (
    .A(multiplexador_1_saida1[3]), .B(multiplexador_1_saida2[3]), .cin(somador_3_cout), .result(saida[3]),
    .cout(somador_4_cout));
  somador somador_5 (
    .A(multiplexador_1_saida1[4]), .B(multiplexador_1_saida2[4]), .cin(somador_4_cout), .result(saida[4]),
    .cout(somador_5_cout));
  somador somador_6 (
    .A(multiplexador_1_saida1[5]), .B(multiplexador_1_saida2[5]), .cin(somador_5_cout), .result(saida[5]),
    .cout(somador_6_cout));
  somador somador_7 (
    .A(multiplexador_1_saida1[6]), .B(multiplexador_1_saida2[6]), .cin(somador_6_cout), .result(saida[6]),
    .cout(somador_7_cout));
  somador somador_8 (
    .A(multiplexador_1_saida1[7]), .B(multiplexador_1_saida2[7]), .cin(somador_7_cout), .result(saida[7]),
    .cout(cout));
endmodule

module decoder_1 (
  input  [3:0] seletor,
  input  Enable,
  output AND0,
  output OR1,
  output NOT2,
  output NOR3,
  output NAND4,
  output XOR5,
  output SHIFTe6,
  output SHIFTd7,
  output soma8,
  output sub9
);

  wire and_1_out, and_2_out, and_3_out, and_4_out, and_5_out, and_6_out, and_7_out, and_8_out, and_9_out,
       and_10_out;

  and and_1 (and_1_out, ~seletor[0], ~seletor[1], ~seletor[2], ~seletor[3]);  // AND_Gate
  and and_2 (and_2_out, seletor[0], ~seletor[1], ~seletor[2], ~seletor[3]);  // AND_Gate
  and and_3 (and_3_out, ~seletor[0], seletor[1], ~seletor[2], ~seletor[3]);  // AND_Gate
  and and_4 (and_4_out, seletor[0], seletor[1], ~seletor[2], ~seletor[3]);  // AND_Gate
  and and_5 (and_5_out, ~seletor[0], ~seletor[1], seletor[2], ~seletor[3]);  // AND_Gate
  and and_6 (and_6_out, seletor[0], ~seletor[1], seletor[2], ~seletor[3]);  // AND_Gate
  and and_7 (and_7_out, ~seletor[3], seletor[1], seletor[2], ~seletor[0]);  // AND_Gate
  and and_8 (and_8_out, seletor[0], seletor[1], seletor[2], ~seletor[3]);  // AND_Gate
  and and_9 (and_9_out, ~seletor[0], ~seletor[1], ~seletor[2], seletor[3]);  // AND_Gate
  and and_10 (and_10_out, seletor[0], ~seletor[1], ~seletor[2], seletor[3]);  // AND_Gate
  and and_11 (AND0, and_1_out, Enable);
  and and_12 (OR1, and_2_out, Enable);
  and and_13 (NOT2, and_3_out, Enable);
  and and_14 (NOR3, and_4_out, Enable);
  and and_15 (NAND4, and_5_out, Enable);
  and and_16 (XOR5, and_6_out, Enable);
  and and_17 (SHIFTe6, and_7_out, Enable);
  and and_18 (SHIFTd7, and_8_out, Enable);
  and and_19 (soma8, and_9_out, Enable);
  and and_20 (sub9, and_10_out, Enable);
endmodule

module multiplexador (
  input  [7:0] i1,
  input  [7:0] i2,
  input  choice,
  output [7:0] saida1,
  output [7:0] saida2
);

  and and_1 (saida1[0], i1[0], choice);
  and and_2 (saida1[1], i1[1], choice);
  and and_3 (saida1[2], i1[2], choice);
  and and_4 (saida1[3], i1[3], choice);
  and and_5 (saida1[4], i1[4], choice);
  and and_6 (saida1[5], i1[5], choice);
  and and_7 (saida1[6], i1[6], choice);
  and and_8 (saida1[7], i1[7], choice);
  and and_9 (saida2[0], i2[0], choice);
  and and_10 (saida2[1], i2[1], choice);
  and and_11 (saida2[2], i2[2], choice);
  and and_12 (saida2[3], i2[3], choice);
  and and_13 (saida2[4], i2[4], choice);
  and and_14 (saida2[5], i2[5], choice);
  and and_15 (saida2[6], i2[6], choice);
  and and_16 (saida2[7], i2[7], choice);
endmodule

module AND0 (
  input  [7:0] input1,
  input  [7:0] input2,
  input  choice,
  output [7:0] out_4
);

  wire [7:0] multiplexador_1_saida1, multiplexador_1_saida2;

  multiplexador multiplexador_1 (
    .i1(input1), .i2(input2), .choice(choice), .saida1(multiplexador_1_saida1),
    .saida2(multiplexador_1_saida2));
  and and_1 (out_4[0], multiplexador_1_saida1[0], multiplexador_1_saida2[0]);
  and and_2 (out_4[1], multiplexador_1_saida1[1], multiplexador_1_saida2[1]);
  and and_3 (out_4[2], multiplexador_1_saida1[2], multiplexador_1_saida2[2]);
  and and_4 (out_4[3], multiplexador_1_saida1[3], multiplexador_1_saida2[3]);
  and and_5 (out_4[4], multiplexador_1_saida1[4], multiplexador_1_saida2[4]);
  and and_6 (out_4[5], multiplexador_1_saida1[5], multiplexador_1_saida2[5]);
  and and_7 (out_4[6], multiplexador_1_saida1[6], multiplexador_1_saida2[6]);
  and and_8 (out_4[7], multiplexador_1_saida1[7], multiplexador_1_saida2[7]);
endmodule

module OR1 (
  input  [7:0] input1,
  input  [7:0] input2,
  input  choice,
  output [7:0] out_4
);

  wire [7:0] multiplexador_1_saida1, multiplexador_1_saida2;

  multiplexador multiplexador_1 (
    .i1(input1), .i2(input2), .choice(choice), .saida1(multiplexador_1_saida1),
    .saida2(multiplexador_1_saida2));
  or or_1 (out_4[0], multiplexador_1_saida1[0], multiplexador_1_saida2[0]);
  or or_2 (out_4[1], multiplexador_1_saida1[1], multiplexador_1_saida2[1]);
  or or_3 (out_4[2], multiplexador_1_saida1[2], multiplexador_1_saida2[2]);
  or or_4 (out_4[3], multiplexador_1_saida1[3], multiplexador_1_saida2[3]);
  or or_5 (out_4[4], multiplexador_1_saida1[4], multiplexador_1_saida2[4]);
  or or_6 (out_4[5], multiplexador_1_saida1[5], multiplexador_1_saida2[5]);
  or or_7 (out_4[6], multiplexador_1_saida1[6], multiplexador_1_saida2[6]);
  or or_8 (out_4[7], multiplexador_1_saida1[7], multiplexador_1_saida2[7]);
endmodule

module NOT2 (
  input  [7:0] input1,
  input  choice,
  output [7:0] saida
);

  wire and_1_out, and_2_out, and_3_out, and_4_out, and_5_out, and_6_out, and_7_out, and_8_out;

  and and_1 (and_1_out, input1[0], choice);
  and and_2 (and_2_out, input1[1], choice);
  and and_3 (and_3_out, input1[2], choice);
  and and_4 (and_4_out, input1[3], choice);
  and and_5 (and_5_out, input1[4], choice);
  and and_6 (and_6_out, input1[5], choice);
  and and_7 (and_7_out, input1[6], choice);
  and and_8 (and_8_out, input1[7], choice);
  not not_1 (saida[0], and_1_out);
  not not_2 (saida[1], and_2_out);
  not not_3 (saida[2], and_3_out);
  not not_4 (saida[3], and_4_out);
  not not_5 (saida[4], and_5_out);
  not not_6 (saida[5], and_6_out);
  not not_7 (saida[6], and_7_out);
  not not_8 (saida[7], and_8_out);
endmodule

module NOR3 (
  input  [7:0] input1,
  input  [7:0] input2,
  input  choice,
  output [7:0] out_4
);

  wire or_1_out, or_2_out, or_3_out, or_4_out, or_5_out, or_6_out, or_7_out, or_8_out;
  wire [7:0] multiplexador_1_saida1, multiplexador_1_saida2;

  multiplexador multiplexador_1 (
    .i1(input1), .i2(input2), .choice(choice), .saida1(multiplexador_1_saida1),
    .saida2(multiplexador_1_saida2));
  or or_1 (or_1_out, multiplexador_1_saida1[0], multiplexador_1_saida2[0]);
  not not_1 (out_4[0], or_1_out);
  or or_2 (or_2_out, multiplexador_1_saida1[1], multiplexador_1_saida2[1]);
  not not_2 (out_4[1], or_2_out);
  or or_3 (or_3_out, multiplexador_1_saida1[2], multiplexador_1_saida2[2]);
  not not_3 (out_4[2], or_3_out);
  or or_4 (or_4_out, multiplexador_1_saida1[3], multiplexador_1_saida2[3]);
  not not_4 (out_4[3], or_4_out);
  or or_5 (or_5_out, multiplexador_1_saida1[4], multiplexador_1_saida2[4]);
  not not_5 (out_4[4], or_5_out);
  or or_6 (or_6_out, multiplexador_1_saida1[5], multiplexador_1_saida2[5]);
  not not_6 (out_4[5], or_6_out);
  or or_7 (or_7_out, multiplexador_1_saida1[6], multiplexador_1_saida2[6]);
  not not_7 (out_4[6], or_7_out);
  or or_8 (or_8_out, multiplexador_1_saida1[7], multiplexador_1_saida2[7]);
  not not_8 (out_4[7], or_8_out);
endmodule

module NAND4 (
  input  [7:0] input1,
  input  [7:0] input2,
  input  choice,
  output [7:0] out_4
);

  wire and_1_out, and_2_out, and_3_out, and_4_out, and_5_out, and_6_out, and_7_out, and_8_out;
  wire [7:0] multiplexador_1_saida1, multiplexador_1_saida2;

  multiplexador multiplexador_1 (
    .i1(input1), .i2(input2), .choice(choice), .saida1(multiplexador_1_saida1),
    .saida2(multiplexador_1_saida2));
  and and_1 (and_1_out, multiplexador_1_saida1[0], multiplexador_1_saida2[0]);
  not not_1 (out_4[0], and_1_out);
  and and_2 (and_2_out, multiplexador_1_saida1[1], multiplexador_1_saida2[1]);
  not not_2 (out_4[1], and_2_out);
  and and_3 (and_3_out, multiplexador_1_saida1[2], multiplexador_1_saida2[2]);
  not not_3 (out_4[2], and_3_out);
  and and_4 (and_4_out, multiplexador_1_saida1[3], multiplexador_1_saida2[3]);
  not not_4 (out_4[3], and_4_out);
  and and_5 (and_5_out, multiplexador_1_saida1[4], multiplexador_1_saida2[4]);
  not not_5 (out_4[4], and_5_out);
  and and_6 (and_6_out, multiplexador_1_saida1[5], multiplexador_1_saida2[5]);
  not not_6 (out_4[5], and_6_out);
  and and_7 (and_7_out, multiplexador_1_saida1[6], multiplexador_1_saida2[6]);
  not not_7 (out_4[6], and_7_out);
  and and_8 (and_8_out, multiplexador_1_saida1[7], multiplexador_1_saida2[7]);
  not not_8 (out_4[7], and_8_out);
endmodule

module shiftE6 (
  input  [7:0] input1,
  input  [7:0] input2,
  input  choice,
  output [7:0] saida,
  output [7:0] saida2
);

  wire [7:7] multiplexador_1_saida1, multiplexador_1_saida2;

  multiplexador multiplexador_1 (
    .i1(input1), .i2(input2), .choice(choice), .saida1({multiplexador_1_saida1[7], saida[7:1]}),
    .saida2({multiplexador_1_saida2[7], saida2[7:1]}));

  assign saida[0] = 1'b0;
  assign saida2[0] = 1'b0;
endmodule

module shifte6_p2 (
  input  [7:0] input1,
  input  [7:0] input2,
  input  choice,
  output [7:0] saida1,
  output [7:0] saida2
);

  wire [7:0] shifte6_1_saida, shifte6_1_saida2;

  shiftE6 shifte6_1 (
    .input1(input1), .input2(input2), .choice(choice), .saida(shifte6_1_saida), .saida2(shifte6_1_saida2));
  shiftE6 shifte6_2 (
    .input1(shifte6_1_saida), .input2(shifte6_1_saida2), .choice(choice), .saida(saida1), .saida2(saida2));
endmodule

module shiftd7 (
  input  [7:0] input1,
  input  [7:0] input2,
  input  choice,
  output [7:0] saida,
  output [7:0] saida2
);

  wire [0:0] multiplexador_1_saida1, multiplexador_1_saida2;

  multiplexador multiplexador_1 (
    .i1(input1), .i2(input2), .choice(choice), .saida1({saida[6:0], multiplexador_1_saida1[0]}),
    .saida2({saida2[6:0], multiplexador_1_saida2[0]}));

  assign saida[7] = 1'b0;
  assign saida2[7] = 1'b0;
endmodule

module shiftd7_p2 (
  input  [7:0] input1,
  input  [7:0] input2,
  input  choice,
  output [7:0] saida1,
  output [7:0] saida2
);

  wire [7:0] shiftd7_1_saida, shiftd7_1_saida2;

  shiftd7 shiftd7_1 (
    .input1(input1), .input2(input2), .choice(choice), .saida(shiftd7_1_saida), .saida2(shiftd7_1_saida2));
  shiftd7 shiftd7_2 (
    .input1(shiftd7_1_saida), .input2(shiftd7_1_saida2), .choice(choice), .saida(saida1), .saida2(saida2));
endmodule

module XOR5 (
  input  [7:0] input1,
  input  [7:0] input2,
  input  choice,
  output [7:0] out_4
);

  wire [7:0] multiplexador_1_saida1, multiplexador_1_saida2;

  multiplexador multiplexador_1 (
    .i1(input1), .i2(input2), .choice(choice), .saida1(multiplexador_1_saida1),
    .saida2(multiplexador_1_saida2));
  xor xor_1 (out_4[0], multiplexador_1_saida1[0], multiplexador_1_saida2[0]);
  xor xor_2 (out_4[1], multiplexador_1_saida1[1], multiplexador_1_saida2[1]);
  xor xor_3 (out_4[2], multiplexador_1_saida1[2], multiplexador_1_saida2[2]);
  xor xor_4 (out_4[3], multiplexador_1_saida1[3], multiplexador_1_saida2[3]);
  xor xor_5 (out_4[4], multiplexador_1_saida1[4], multiplexador_1_saida2[4]);
  xor xor_6 (out_4[5], multiplexador_1_saida1[5], multiplexador_1_saida2[5]);
  xor xor_7 (out_4[6], multiplexador_1_saida1[6], multiplexador_1_saida2[6]);
  xor xor_8 (out_4[7], multiplexador_1_saida1[7], multiplexador_1_saida2[7]);
endmodule

module subtrator (
  input  [7:0] input1,
  input  [7:0] input2,
  input  choice,
  output [7:0] saida,
  output cout
);

  wire somador8bits_plus1_1_cout;
  wire [7:0] not2_1_saida, somador8bits_plus1_1_saida;

  NOT2 not2_1 (.input1(input2), .choice(choice), .saida(not2_1_saida));
  somador8bits_plus1 somador8bits_plus1_1 (
    .input1(not2_1_saida), .choice(choice), .saida(somador8bits_plus1_1_saida),
    .cout(somador8bits_plus1_1_cout));
  somador8bits_semTerra somador8bits_semterra_1 (
    .cin(somador8bits_plus1_1_cout), .input1(input1), .input2(somador8bits_plus1_1_saida), .choice(choice),
    .saida(saida), .cout(cout));
endmodule

module somador8bits_plus1 (
  input  [7:0] input1,
  input  choice,
  output [7:0] saida,
  output cout
);

  wire somador_1_cout, somador_2_cout, somador_3_cout, somador_4_cout, somador_5_cout, somador_6_cout,
       somador_7_cout;
  wire [7:0] multiplexador_1_saida1, multiplexador_1_saida2;

  multiplexador multiplexador_1 (
    .i1(input1), .i2(8'h1), .choice(choice), .saida1(multiplexador_1_saida1), .saida2(multiplexador_1_saida2));
  somador somador_1 (
    .A(multiplexador_1_saida1[0]), .B(multiplexador_1_saida2[0]), .cin(1'b0), .result(saida[0]),
    .cout(somador_1_cout));
  somador somador_2 (
    .A(multiplexador_1_saida1[1]), .B(multiplexador_1_saida2[1]), .cin(somador_1_cout), .result(saida[1]),
    .cout(somador_2_cout));
  somador somador_3 (
    .A(multiplexador_1_saida1[2]), .B(multiplexador_1_saida2[2]), .cin(somador_2_cout), .result(saida[2]),
    .cout(somador_3_cout));
  somador somador_4 (
    .A(multiplexador_1_saida1[3]), .B(multiplexador_1_saida2[3]), .cin(somador_3_cout), .result(saida[3]),
    .cout(somador_4_cout));
  somador somador_5 (
    .A(multiplexador_1_saida1[4]), .B(multiplexador_1_saida2[4]), .cin(somador_4_cout), .result(saida[4]),
    .cout(somador_5_cout));
  somador somador_6 (
    .A(multiplexador_1_saida1[5]), .B(multiplexador_1_saida2[5]), .cin(somador_5_cout), .result(saida[5]),
    .cout(somador_6_cout));
  somador somador_7 (
    .A(multiplexador_1_saida1[6]), .B(multiplexador_1_saida2[6]), .cin(somador_6_cout), .result(saida[6]),
    .cout(somador_7_cout));
  somador somador_8 (
    .A(multiplexador_1_saida1[7]), .B(multiplexador_1_saida2[7]), .cin(somador_7_cout), .result(saida[7]),
    .cout(cout));
endmodule

module somador8bits_semTerra (
  input  cin,
  input  [7:0] input1,
  input  [7:0] input2,
  input  choice,
  output [7:0] saida,
  output cout
);

  wire somador_1_cout, somador_2_cout, somador_3_cout, somador_4_cout, somador_5_cout, somador_6_cout,
       somador_7_cout;
  wire [7:0] multiplexador_1_saida1, multiplexador_1_saida2;

  multiplexador multiplexador_1 (
    .i1(input1), .i2(input2), .choice(choice), .saida1(multiplexador_1_saida1),
    .saida2(multiplexador_1_saida2));
  somador somador_1 (
    .A(multiplexador_1_saida1[0]), .B(multiplexador_1_saida2[0]), .cin(cin), .result(saida[0]),
    .cout(somador_1_cout));
  somador somador_2 (
    .A(multiplexador_1_saida1[1]), .B(multiplexador_1_saida2[1]), .cin(somador_1_cout), .result(saida[1]),
    .cout(somador_2_cout));
  somador somador_3 (
    .A(multiplexador_1_saida1[2]), .B(multiplexador_1_saida2[2]), .cin(somador_2_cout), .result(saida[2]),
    .cout(somador_3_cout));
  somador somador_4 (
    .A(multiplexador_1_saida1[3]), .B(multiplexador_1_saida2[3]), .cin(somador_3_cout), .result(saida[3]),
    .cout(somador_4_cout));
  somador somador_5 (
    .A(multiplexador_1_saida1[4]), .B(multiplexador_1_saida2[4]), .cin(somador_4_cout), .result(saida[4]),
    .cout(somador_5_cout));
  somador somador_6 (
    .A(multiplexador_1_saida1[5]), .B(multiplexador_1_saida2[5]), .cin(somador_5_cout), .result(saida[5]),
    .cout(somador_6_cout));
  somador somador_7 (
    .A(multiplexador_1_saida1[6]), .B(multiplexador_1_saida2[6]), .cin(somador_6_cout), .result(saida[6]),
    .cout(somador_7_cout));
  somador somador_8 (
    .A(multiplexador_1_saida1[7]), .B(multiplexador_1_saida2[7]), .cin(somador_7_cout), .result(saida[7]),
    .cout(cout));
endmodule
