// Logisim project circuito_sem_e_com_otimizacao.circ as structural Verilog: 3 circuits, main circuit main
module main (
  input  [2:0] ABC,
  input  [2:0] abcOPT,
  output O,
  output oOPT
);

  wire and_1_out, and_2_out, and_3_out, and_4_out, and_5_out, and_6_out, and_7_out, and_8_out, and_9_out,
       not_1_out, not_2_out, not_3_out, not_4_out, not_5_out, not_6_out, not_7_out, not_8_out, not_9_out,
       not_10_out, not_11_out;

  not not_1 (not_1_out, ABC[2]);
  not not_2 (not_2_out, ABC[1]);
  not not_3 (not_3_out, ABC[2]);
  not not_4 (not_4_out, ABC[0]);
  not not_5 (not_5_out, ABC[1]);
  not not_6 (not_6_out, ABC[0]);
  not not_7 (not_7_out, ABC[1]);
  not not_8 (not_8_out, abcOPT[1]);
  not not_9 (not_9_out, abcOPT[1]);
  not not_10 (not_10_out, abcOPT[2]);
  not not_11 (not_11_out, abcOPT[0]);
  and and_1 (and_1_out, not_1_out, not_2_out, ABC[0]);
  and and_2 (and_2_out, not_3_out, ABC[1], not_4_out);
  and and_3 (and_3_out, ABC[2], not_5_out, not_6_out);
  and and_4 (and_4_out, ABC[2], not_7_out, ABC[0]);
  and and_5 (and_5_out, ABC[2], ABC[1], ABC[0]);
  and and_6 (and_6_out, abcOPT[2], not_8_out);
  and and_7 (and_7_out, abcOPT[2], abcOPT[0]);
  and and_8 (and_8_out, not_9_out, abcOPT[0]);
  and and_9 (and_9_out, not_10_out, abcOPT[1], not_11_out);
  or or_1 (O, and_1_out, and_2_out, and_3_out, and_4_out, and_5_out);
  or or_2 (oOPT, and_6_out, and_7_out, and_8_out, and_9_out);

  // Notes on the sheet:
  //   Digamos que temos o seguinte problema:
  //   A || B || C || F(A,B,C)
  //   0     0     0           0
  //   0     0     1           1
  //   0     1     0           1
  //   0     1     1           0
  //   1     0     0           1
  //   1     0     1           1
  //   1     1     0           0
  //   1     1     1           1
  //   Sem Optimização
  //   Com Optimização
endmodule

module SemOptimizacao (
  input  [2:0] ABC,
  output O
);

  wire and_1_out, and_2_out, and_3_out, and_4_out, and_5_out, not_1_out, not_2_out, not_3_out, not_4_out,
       not_5_out, not_6_out, not_7_out;

  not not_1 (not_1_out, ABC[2]);
  not not_2 (not_2_out, ABC[1]);
  not not_3 (not_3_out, ABC[2]);
  not not_4 (not_4_out, ABC[0]);
  not not_5 (not_5_out, ABC[1]);
  not not_6 (not_6_out, ABC[0]);
  not not_7 (not_7_out, ABC[1]);
  and and_1 (and_1_out, not_1_out, not_2_out, ABC[0]);
  and and_2 (and_2_out, not_3_out, ABC[1], not_4_out);
  and and_3 (and_3_out, ABC[2], not_5_out, not_6_out);
  and and_4 (and_4_out, ABC[2], not_7_out, ABC[0]);
  and and_5 (and_5_out, ABC[2], ABC[1], ABC[0]);
  or or_1 (O, and_1_out, and_2_out, and_3_out, and_4_out, and_5_out);
endmodule

module ComOptimizacao (
  input  [2:0] abcOPT,
  output oOPT
);

  wire and_1_out, and_2_out, and_3_out, and_4_out, not_1_out, not_2_out, not_3_out, not_4_out;

  not not_1 (not_1_out, abcOPT[1]);
  not not_2 (not_2_out, abcOPT[1]);
  not not_3 (not_3_out, abcOPT[2]);
  not not_4 (not_4_out, abcOPT[0]);
  and and_1 (and_1_out, abcOPT[2], not_1_out);
  and and_2 (and_2_out, abcOPT[2], abcOPT[0]);
  and and_3 (and_3_out, not_2_out, abcOPT[0]);
  and and_4 (and_4_out, not_3_out, abcOPT[1], not_4_out);
  or or_1 (oOPT, and_1_out, and_2_out, and_3_out, and_4_out);
endmodule
