// Logisim project contador_sincrono.circ as structural Verilog: 4 circuits, main circuit SRLatch
module SRLatch (
  input  S,
  input  R,
  output Q,
  output Qb
);

  nand nand_1 (Q, S, Qb);
  nand nand_2 (Qb, Q, R);
endmodule

module DFlipFlop (
  input  D,
  input  Enable,
  input  CLK,
  output Q,
  output Qb
);

  wire and_1_out, nand_1_out, nand_2_out, nand_3_out, nand_4_out, not_1_out, not_2_out, not_3_out,
       srlatch_1_q;

  and and_1 (and_1_out, D, Enable);
  not not_1 (not_1_out, and_1_out);
  nand nand_1 (nand_1_out, and_1_out, CLK);
  nand nand_2 (nand_2_out, CLK, not_1_out);
  not not_2 (not_2_out, CLK);
  SRLatch srlatch_1 (.S(nand_1_out), .R(nand_2_out), .Q(srlatch_1_q));  // open: Qb
  not not_3 (not_3_out, srlatch_1_q);
  nand nand_3 (nand_3_out, srlatch_1_q, not_2_out);
  nand nand_4 (nand_4_out, not_2_out, not_3_out);
  SRLatch srlatch_2 (.S(nand_3_out), .R(nand_4_out), .Q(Q), .Qb(Qb));
endmodule

module JKFlipFlop (
  input  J,
  input  Enable,
  input  CLK,
  input  K,
  output Q,
  output Qb
);

  wire and_1_out, and_2_out, and_3_out, and_4_out, or_1_out;

  and and_1 (and_1_out, J, Enable);
  and and_2 (and_2_out, Enable, K);
  and and_3 (and_3_out, Qb, and_1_out);
  and and_4 (and_4_out, ~and_2_out, Q);  // AND_Gate
  or or_1 (or_1_out, and_3_out, and_4_out);
  DFlipFlop dflipflop_1 (.Enable(Enable), .D(or_1_out), .CLK(CLK), .Q(Q), .Qb(Qb));
endmodule

module ContadorSincrono (
  input  Enable,
  output [3:0] out_2
);

  wire and_1_out, and_2_out, clock_1_out;

  Clock clock_1 (.out(clock_1_out));
  JKFlipFlop jkflipflop_1 (.Enable(Enable), .K(1'b1), .J(1'b1), .CLK(clock_1_out), .Q(out_2[0]));  // open: Qb
  JKFlipFlop jkflipflop_2 (.Enable(Enable), .K(out_2[0]), .J(out_2[0]), .CLK(clock_1_out), .Q(out_2[1]));  // open: Qb
  and and_1 (and_1_out, out_2[0], out_2[1]);
  JKFlipFlop jkflipflop_3 (.Enable(Enable), .K(and_1_out), .J(and_1_out), .CLK(clock_1_out), .Q(out_2[2]));  // open: Qb
  and and_2 (and_2_out, and_1_out, out_2[2]);
  JKFlipFlop jkflipflop_4 (.Enable(Enable), .K(and_2_out), .J(and_2_out), .CLK(clock_1_out), .Q(out_2[3]));  // open: Qb
endmodule
