// Logisim project detector_primo.circ as structural Verilog: 1 circuit, main circuit main
module main (
  input  [3:0] ABCD,
  output out_2
);

  wire and_1_out, and_2_out, and_3_out, and_4_out, not_1_out, not_2_out, not_3_out, not_4_out, not_5_out;

  not not_1 (not_1_out, ABCD[1]);
  not not_2 (not_2_out, ABCD[2]);
  not not_3 (not_3_out, ABCD[3]);
  not not_4 (not_4_out, ABCD[3]);
  not not_5 (not_5_out, ABCD[2]);
  and and_1 (and_1_out, ABCD[2], not_1_out, ABCD[0]);
  and and_2 (and_2_out, not_2_out, ABCD[1], ABCD[0]);
  and and_3 (and_3_out, not_3_out, ABCD[2], ABCD[0]);
  and and_4 (and_4_out, not_4_out, not_5_out, ABCD[1]);
  or or_1 (out_2, and_1_out, and_2_out, and_3_out, and_4_out);

  // Notes on the sheet:
  //   Primo = 1 || Não Primo = 0
endmodule
