// Logisim project detector_sequencia_101.circ as structural Verilog: 3 circuits, main circuit main
module main (
  input  [2:0] in_1,
  input  [7:0] DataInput,
  input  Enable,
  output out_4,
  output O
);

  wire and_2_out, and_3_out, and_4_out, and_5_out, and_6_out, and_7_out, clock_1_out, dflipflop_1_q,
       dflipflop_2_q, dflipflop_3_q, dflipflop_4_q, dflipflop_5_q, dflipflop_6_q, dflipflop_7_q,
       dflipflop_8_q, not_1_out, not_2_out, not_3_out, not_4_out, not_5_out, not_6_out, not_7_out;

  Clock clock_1 (.out(clock_1_out));
  not not_1 (not_1_out, in_1[1]);
  and and_1 (out_4, in_1[0], not_1_out, in_1[2]);
  DFlipFlop dflipflop_1 (.Enable(Enable), .D(DataInput[0]), .CLK(clock_1_out), .Q(dflipflop_1_q));  // open: Qb
  DFlipFlop dflipflop_2 (.Enable(Enable), .D(DataInput[1]), .CLK(clock_1_out), .Q(dflipflop_2_q));  // open: Qb
  DFlipFlop dflipflop_3 (.Enable(Enable), .D(DataInput[2]), .CLK(clock_1_out), .Q(dflipflop_3_q));  // open: Qb
  DFlipFlop dflipflop_4 (.Enable(Enable), .D(DataInput[3]), .CLK(clock_1_out), .Q(dflipflop_4_q));  // open: Qb
  DFlipFlop dflipflop_5 (.Enable(Enable), .D(DataInput[4]), .CLK(clock_1_out), .Q(dflipflop_5_q));  // open: Qb
  DFlipFlop dflipflop_6 (.Enable(Enable), .D(DataInput[5]), .CLK(clock_1_out), .Q(dflipflop_6_q));  // open: Qb
  DFlipFlop dflipflop_7 (.Enable(Enable), .D(DataInput[6]), .CLK(clock_1_out), .Q(dflipflop_7_q));  // open: Qb
  DFlipFlop dflipflop_8 (.Enable(Enable), .D(DataInput[7]), .CLK(clock_1_out), .Q(dflipflop_8_q));  // open: Qb
  not not_2 (not_2_out, dflipflop_2_q);
  not not_3 (not_3_out, dflipflop_3_q);
  not not_4 (not_4_out, dflipflop_4_q);
  not not_5 (not_5_out, dflipflop_5_q);
  not not_6 (not_6_out, dflipflop_6_q);
  not not_7 (not_7_out, dflipflop_7_q);
  and and_2 (and_2_out, dflipflop_1_q, not_2_out, dflipflop_3_q);
  and and_3 (and_3_out, dflipflop_2_q, not_3_out, dflipflop_4_q);
  and and_4 (and_4_out, dflipflop_3_q, not_4_out, dflipflop_5_q);
  and and_5 (and_5_out, dflipflop_4_q, not_5_out, dflipflop_6_q);
  and and_6 (and_6_out, dflipflop_5_q, not_6_out, dflipflop_7_q);
  and and_7 (and_7_out, dflipflop_6_q, not_7_out, dflipflop_8_q);
  or or_1 (O, and_2_out, and_3_out, and_4_out, and_5_out, and_6_out, and_7_out);

  // Notes on the sheet:
  //   Condição de Indentificação
endmodule

module SRLatch (
  input  S,
  input  R,
  output Q,
  output Qb
);

  nand nand_1 (Q, S, Qb);
  nand nand_2 (Qb, Q, R);
endmodule

module DFlipFlop (
  input  D,
  input  Enable,
  input  CLK,
  output Q,
  output Qb
);

  wire and_1_out, nand_1_out, nand_2_out, nand_3_out, nand_4_out, not_1_out, not_2_out, not_3_out,
       srlatch_1_q;

  and and_1 (and_1_out, D, Enable);
  not not_1 (not_1_out, and_1_out);
  nand nand_1 (nand_1_out, and_1_out, CLK);
  nand nand_2 (nand_2_out, CLK, not_1_out);
  not not_2 (not_2_out, CLK);
  SRLatch srlatch_1 (.S(nand_1_out), .R(nand_2_out), .Q(srlatch_1_q));  // open: Qb
  not not_3 (not_3_out, srlatch_1_q);
  nand nand_3 (nand_3_out, srlatch_1_q, not_2_out);
  nand nand_4 (nand_4_out, not_2_out, not_3_out);
  SRLatch srlatch_2 (.S(nand_3_out), .R(nand_4_out), .Q(Q), .Qb(Qb));
endmodule
