// Logisim project extensor_sinal_4_to_8.circ as structural Verilog: 1 circuit, main circuit main
module main (
  input  [3:0] in_1,
  output [7:0] out_2
);


  assign out_2 = {{5{in_1[3]}}, in_1[2:0]};
endmodule
