// Logisim project maquinaDeEstado.circ as structural Verilog: 2 circuits, main circuit flip_flop
module flip_flop (
  input  Data,
  input  clock,
  output Q,
  output notQ
);

  wire nand_1_out, nand_2_out, not_1_out;

  not not_1 (not_1_out, Data);
  nand nand_1 (nand_1_out, Data, clock);
  nand nand_2 (nand_2_out, not_1_out, clock);
  nand nand_3 (Q, nand_1_out, notQ);
  nand nand_4 (notQ, Q, nand_2_out);
endmodule

module Maquina (
  input  A,
  input  B,
  input  Z,
  output out_4,
  output out_5,
  output out_6,
  output out_7
);

  wire and_1_out, and_2_out, and_3_out, and_4_out, and_5_out, and_6_out, clock_1_out, not_1_out, not_2_out,
       or_1_out, or_2_out;

  not not_1 (not_1_out, Z);
  not not_2 (not_2_out, B);
  and and_1 (and_1_out, not_1_out, ~B);  // AND_Gate
  and and_2 (and_2_out, Z, ~A);  // AND_Gate
  and and_3 (and_3_out, Z, ~B, ~A);  // AND_Gate
  and and_4 (and_4_out, not_1_out, ~A, B);  // AND_Gate
  and and_5 (and_5_out, Z, A, B);
  and and_6 (and_6_out, not_1_out, A, not_2_out);
  or or_1 (or_1_out, and_3_out, and_4_out, and_5_out, and_6_out);
  or or_2 (or_2_out, and_1_out, and_2_out);
  Clock clock_1 (.out(clock_1_out));
  flip_flop flip_flop_1 (.Data(or_2_out), .clock(clock_1_out), .Q(out_4), .notQ(out_5));
  flip_flop flip_flop_2 (.Data(or_1_out), .clock(clock_1_out), .Q(out_6), .notQ(out_7));
endmodule
