// Logisim project memoria_rom_8_bits.circ as structural Verilog: 1 circuit, main circuit main
module main (
  input  [2:0] Address,
  output [7:0] Data
);

  wire and_1_out, and_2_out, and_3_out, and_4_out, and_5_out, and_6_out, and_8_out;

  and and_1 (and_1_out, ~Address[2], ~Address[1], ~Address[0]);  // AND_Gate
  and and_2 (and_2_out, ~Address[2], ~Address[1], Address[0]);  // AND_Gate
  and and_3 (and_3_out, ~Address[2], Address[1], ~Address[0]);  // AND_Gate
  and and_4 (and_4_out, ~Address[2], Address[1], Address[0]);  // AND_Gate
  and and_5 (and_5_out, Address[2], ~Address[1], ~Address[0]);  // AND_Gate
  and and_6 (and_6_out, Address[2], ~Address[1], Address[0]);  // AND_Gate
  // AND_Gate and_7 has open pins: in0=Address[2], in1=Address[1], in2=Address[0], out=open
  and and_8 (and_8_out, Address[2], Address[1], Address[0]);
  or or_1 (Data[7], and_8_out, and_4_out, and_3_out, and_1_out);
  or or_2 (Data[6], and_8_out, and_6_out, and_1_out);
  or or_3 (Data[5], and_8_out, and_6_out, and_4_out, and_2_out);
  or or_4 (Data[4], and_6_out, and_5_out, and_2_out, and_1_out);
  or or_5 (Data[3], and_8_out, and_6_out, and_5_out, and_4_out, and_2_out, and_1_out);
  or or_6 (Data[2], and_8_out, and_4_out, and_3_out, and_1_out);
  or or_7 (Data[1], and_6_out, and_4_out, and_2_out, and_1_out);
  or or_8 (Data[0], and_8_out, and_6_out, and_5_out, and_4_out, and_3_out);

  // Notes on the sheet:
  //   000                   11011110
  //   001                   00111010
  //   010                   10000101
  //   011                   10101111
  //   100                   00011001
  //   101                   01111011
  //   110                   00000000
  //   111                   11101101
endmodule
