// Logisim project porta_xor_and_not_or.circ as structural Verilog: 1 circuit, main circuit main
module main (
  input  A,
  input  B,
  output out_3
);

  wire AND1_out, AND2_out, not_1_out, not_2_out;

  not not_1 (not_1_out, B);
  not not_2 (not_2_out, A);
  and AND1 (AND1_out, A, not_1_out);
  and AND2 (AND2_out, not_2_out, B);
  or or_1 (out_3, AND1_out, AND2_out);
endmodule
