// Logisim project somador-8-bits.circ as structural Verilog: 3 circuits, main circuit somador1bit
module somador1bit (
  input  A0,
  input  B0,
  input  cin,
  output sum,
  output cout
);

  wire and_1_out, and_2_out, and_3_out, xor_1_out;

  and and_1 (and_1_out, A0, B0);
  and and_2 (and_2_out, A0, cin);
  and and_3 (and_3_out, B0, cin);
  xor xor_1 (xor_1_out, A0, B0);
  xor xor_2 (sum, xor_1_out, cin);
  or or_1 (cout, and_1_out, and_2_out, and_3_out);
endmodule

module somador4bit (
  input  A3,
  input  A2,
  input  A1,
  input  AO,
  input  B3,
  input  B2,
  input  B1,
  input  B0,
  input  cin,
  output C3,
  output C2,
  output C1,
  output C0,
  output cout
);

  wire somador1bit_2_cout, somador1bit_3_cout, somador1bit_4_cout;

  somador1bit somador1bit_1 (.A0(A3), .B0(B3), .cin(somador1bit_2_cout), .sum(C3), .cout(cout));
  somador1bit somador1bit_2 (.A0(A2), .B0(B2), .cin(somador1bit_3_cout), .sum(C2), .cout(somador1bit_2_cout));
  somador1bit somador1bit_3 (.A0(A1), .B0(B1), .cin(somador1bit_4_cout), .sum(C1), .cout(somador1bit_3_cout));
  somador1bit somador1bit_4 (.A0(AO), .B0(B0), .cin(cin), .sum(C0), .cout(somador1bit_4_cout));
endmodule

module somador8bit (
  input  in_1,
  input  in_2,
  input  in_3,
  input  in_4,
  input  in_5,
  input  in_6,
  input  in_7,
  input  in_8,
  input  in_9,
  input  in_10,
  input  in_11,
  input  in_12,
  input  in_13,
  input  in_14,
  input  in_15,
  input  in_16,
  output out_17,
  output out_18,
  output out_19,
  output out_20,
  output out_21,
  output out_22,
  output out_23,
  output out_24,
  output out_25
);

  wire somador4bit_2_cout;

  somador4bit somador4bit_1 (
    .A3(in_2), .A2(in_3), .A1(in_4), .AO(in_5), .B3(in_10), .B2(in_11), .B1(in_12), .B0(in_13),
    .cin(somador4bit_2_cout), .C3(out_19), .C2(out_20), .C1(out_21), .C0(out_22), .cout(out_17));
  somador4bit somador4bit_2 (
    .A3(in_6), .A2(in_7), .A1(in_8), .AO(in_1), .B3(in_14), .B2(in_15), .B1(in_16), .B0(in_9), .cin(1'b0),
    .C3(out_23), .C2(out_24), .C1(out_25), .C0(out_18), .cout(somador4bit_2_cout));
endmodule
