// Logisim project sr_latch_flipflop_d_flipflop_jk.circ as structural Verilog: 3 circuits, main circuit SRLatch1
module SRLatch1 (
  input  S,
  input  R,
  output Q,
  output Qb
);

  nand nand_1 (Q, S, Qb);
  nand nand_2 (Qb, Q, R);
endmodule

module DFlipFlop1 (
  input  D,
  input  Enable,
  input  CLK,
  output Q,
  output Qb
);

  wire and_1_out, nand_1_out, nand_2_out, nand_3_out, nand_4_out, not_1_out, not_2_out, not_3_out,
       srlatch1_1_q;

  and and_1 (and_1_out, D, Enable);
  not not_1 (not_1_out, and_1_out);
  nand nand_1 (nand_1_out, and_1_out, CLK);
  nand nand_2 (nand_2_out, CLK, not_1_out);
  not not_2 (not_2_out, CLK);
  SRLatch1 srlatch1_1 (.S(nand_1_out), .R(nand_2_out), .Q(srlatch1_1_q));  // open: Qb
  not not_3 (not_3_out, srlatch1_1_q);
  nand nand_3 (nand_3_out, srlatch1_1_q, not_2_out);
  nand nand_4 (nand_4_out, not_2_out, not_3_out);
  SRLatch1 srlatch1_2 (.S(nand_3_out), .R(nand_4_out), .Q(Q), .Qb(Qb));
endmodule

module JKFlipFlop1 (
  input  J,
  input  Enable,
  input  CLK,
  input  K,
  output Q,
  output Qb
);

  wire and_1_out, and_2_out, and_3_out, and_4_out, or_1_out;

  and and_1 (and_1_out, J, Enable);
  and and_2 (and_2_out, Enable, K);
  and and_3 (and_3_out, Qb, and_1_out);
  and and_4 (and_4_out, ~and_2_out, Q);  // AND_Gate
  or or_1 (or_1_out, and_3_out, and_4_out);
  DFlipFlop1 dflipflop1_1 (.Enable(Enable), .D(or_1_out), .CLK(CLK), .Q(Q), .Qb(Qb));
endmodule
